# Fritzing sketch keyboard (saved by Fritzing 0.9.4)

parts:
  R11 = Resistor [tolerance=±5% resistance=100 package=THT]
  LED2 = RGB LED (com. anode, rbg) [package="5 mm [THT]"]
  R10 = Resistor [tolerance=±5% resistance=100 package=THT]
  R7 = Resistor [tolerance=±5% resistance=150 package=THT]
  R3 = Resistor [tolerance=±5% resistance=1k package=THT]
  R4 = Resistor [tolerance=±5% resistance=100 package=THT]
  LED3 = RGB LED (com. anode, rbg) [package="5 mm [THT]"]
  R2 = Resistor [tolerance=±5% resistance=1k package=THT]
  R9 = Resistor [tolerance=±5% resistance=150 package=THT]
  R5 = Resistor [tolerance=±5% resistance=150 package=THT]
  R1 = Resistor [tolerance=±5% resistance=1k package=THT]
  R8 = Resistor [tolerance=±5% resistance=100 package=THT]
  Q3 = NPN-Transistor [package="TO92 [THT]"]
  R6 = Resistor [tolerance=±5% resistance=100 package=THT]
  R12 = Resistor [tolerance=±5% resistance=100 package=THT]
  LED1 = RGB LED (com. anode, rbg) [package="5 mm [THT]"]
  Q2 = NPN-Transistor [package="TO92 [THT]"]
  Q1 = NPN-Transistor [package="TO92 [THT]"]

nets:
  N1: R11.Pin_0, R10.Pin_0, R12.Pin_0, Q2.C
  N2: R11.Pin_1, LED2.green_cathode
  N3: LED2.red_cathode, R6.Pin_1
  5V: LED2.common_anode, LED3.common_anode, LED1.common_anode
  N4: LED2.blue_cathode, R7.Pin_1
  N5: R10.Pin_1, LED1.green_cathode
  N6: R7.Pin_0, R9.Pin_0, R5.Pin_0, Q3.C
  N7: R3.Pin_1, Q3.B
  N8: R4.Pin_0, R8.Pin_0, R6.Pin_0, Q1.C
  N9: R4.Pin_1, LED1.red_cathode
  N10: LED3.red_cathode, R8.Pin_1
  N11: LED3.blue_cathode, R9.Pin_1
  N12: LED3.green_cathode, R12.Pin_1
  N13: R2.Pin_1, Q2.B
  N14: R5.Pin_1, LED1.blue_cathode
  N15: R1.Pin_1, Q1.B
  GND: Q3.E, Q2.E, Q1.E
